# Fritzing sketch mini_controller (saved by Fritzing 0.8.7b)
breadboards: 1

parts:
  Part1 = Arduino Uno (Rev3)
  S1 = Pushbutton [package="[THT]"]
  S2 = Pushbutton [package="[THT]"]
  S3 = Pushbutton [package="[THT]"]
  R1 = Resistor [tolerance=±5% resistance=10k package=THT]
  R2 = Resistor [tolerance=±5% resistance=10k package=THT]
  R3 = Resistor [tolerance=±5% resistance=10k package=THT]

nets:
  N1: Part1.D5_PWM, Part1.5V, S1.Pin_3, S1.Pin_4, S2.Pin_1, S2.Pin_2, S3.Pin_1, S3.Pin_2, R1.Pin_1
  N2: Part1.D6_PWM, S2.Pin_3, S2.Pin_4, R2.Pin_1
  N3: Part1.D7, S3.Pin_3, S3.Pin_4, R3.Pin_1
  N4: Part1.GND, R1.Pin_0, R2.Pin_0, R3.Pin_0
  N5: S1.Pin_1, S1.Pin_2
